// Logisim project lab11.circ as structural Verilog
module Ex1 (
  input  [7:0] Input,
  output Out1,
  output [7:0] Out2
);

  and and_1 (Out1, Input[0], Input[7]);
  not not_1 (Out2[7], Input[7]);

  assign Out2[6:0] = Input[6:0];
endmodule

module rotr (
  input  [15:0] A,
  input  [3:0] B,
  output [15:0] Output
);

  wire not_1_out, not_2_out, not_3_out, not_4_out;
  wire [15:0] demultiplexer_1_out0, demultiplexer_1_out1, demultiplexer_2_out0, demultiplexer_2_out1,
       demultiplexer_3_out0, demultiplexer_3_out1, demultiplexer_4_out0, demultiplexer_4_out1,
       multiplexer_2_out, multiplexer_3_out, multiplexer_4_out;

  Demultiplexer #(.width(16), .disabled(0), .enable("false")) demultiplexer_1 (
    .out0(demultiplexer_1_out0), .out1(demultiplexer_1_out1), .in(A), .sel(not_1_out));
  not not_1 (not_1_out, B[0]);
  Demultiplexer #(.width(16), .enable("false")) demultiplexer_2 (
    .out0(demultiplexer_2_out0), .out1(demultiplexer_2_out1), .in(multiplexer_3_out), .sel(not_2_out));
  not not_2 (not_2_out, B[3]);
  Demultiplexer #(.width(16), .enable("false")) demultiplexer_3 (
    .out0(demultiplexer_3_out0), .out1(demultiplexer_3_out1), .in(multiplexer_4_out), .sel(not_3_out));
  not not_3 (not_3_out, B[2]);
  Multiplexer #(.width(16), .disabled(0), .enable("false")) multiplexer_1 (
    .in0(demultiplexer_2_out1), .in1({demultiplexer_2_out0[7:0], demultiplexer_2_out0[15:8]}), .out(Output),
    .sel(B[3]));
  Multiplexer #(.width(16), .disabled(0), .enable("false")) multiplexer_2 (
    .in0(demultiplexer_1_out1), .in1({demultiplexer_1_out0[0], demultiplexer_1_out0[15:1]}),
    .out(multiplexer_2_out), .sel(B[0]));
  Multiplexer #(.width(16), .disabled(0), .enable("false")) multiplexer_3 (
    .in0(demultiplexer_3_out1), .in1({demultiplexer_3_out0[3:0], demultiplexer_3_out0[15:4]}),
    .out(multiplexer_3_out), .sel(B[2]));
  Demultiplexer #(.width(16), .disabled(0), .enable("false")) demultiplexer_4 (
    .out0(demultiplexer_4_out0), .out1(demultiplexer_4_out1), .in(multiplexer_2_out), .sel(not_4_out));
  not not_4 (not_4_out, B[1]);
  Multiplexer #(.width(16), .disabled(0), .enable("false")) multiplexer_4 (
    .in0(demultiplexer_4_out1), .in1({demultiplexer_4_out0[1:0], demultiplexer_4_out0[15:2]}),
    .out(multiplexer_4_out), .sel(B[1]));
endmodule

module fib (
);

  wire clock_1_out;
  wire [31:0] i_q, undriven, undriven_2, undriven_3, undriven_4, x_q, y_q, z_q;

  Clock clock_1 (.out(clock_1_out));
  Register #(.width(32)) i (.D(undriven), .Q(i_q), .clk(clock_1_out));  // open: en, clr
  Register #(.width(32)) x (.D(undriven_2), .Q(x_q), .clk(clock_1_out));  // open: en, clr
  Register #(.width(32)) y (.D(undriven_3), .Q(y_q), .clk(clock_1_out));  // open: en, clr
  Register #(.width(32)) z (.D(undriven_4), .Q(z_q), .clk(clock_1_out));  // open: en, clr
endmodule
